# Fritzing sketch BinaryDisplayTemp (saved by Fritzing 0.4.3b)
breadboards: 1

parts:
  Arduino1 = Arduino
  U1 = 74HC595 [package="DIP16 [THT]"]
  R1 = Resistor [resistance=560 package=THT]
  R1_2 = Resistor [resistance=560 package=THT]
  R1_3 = Resistor [resistance=560 package=THT]
  R1_4 = Resistor [resistance=560 package=THT]
  R1_5 = Resistor [resistance=560 package=THT]
  R1_6 = Resistor [resistance=560 package=THT]
  R1_7 = Resistor [resistance=560 package=THT]
  R1_8 = Resistor [resistance=560 package=THT]
  LED1 = green LED - 5mm
  LED1_2 = green LED - 5mm
  LED1_3 = green LED - 5mm
  LED1_4 = green LED - 5mm
  LED1_5 = green LED - 5mm
  LED1_6 = green LED - 5mm
  LED1_7 = green LED - 5mm
  LED1_8 = green LED - 5mm
  R3 = Temperature Sensor (Thermistor)

nets:
  N1: Arduino1.D4, U1.ST_CP
  N2: Arduino1.D3, U1.SH_CP
  N3: Arduino1.D2, U1.DS
  N4: Arduino1.+5V, U1.MR, U1.Q0, R3.connector0
  GND: Arduino1.GND, U1.GND, U1.OE, R1.Pin_1, R1_2.Pin_1, R1_3.Pin_1, R1_4.Pin_1, R1_5.Pin_1, R1_6.Pin_1, R1_7.Pin_1, R1_8.Pin_1, R3.connector1
  N5: Arduino1.A0, R3.connector2
  N6: U1.Q1, LED1_4.anode
  N7: U1.Q2, LED1_5.anode
  N8: U1.Q3, LED1_6.anode
  N9: U1.Q4, LED1_7.anode
  N10: U1.Q5, LED1_8.anode
  N11: U1.Q6, LED1.anode
  N12: U1.Q7, LED1_2.anode
  N13: U1.VCC, LED1_3.anode
  N14: R1.Pin_0, LED1_3.cathode
  N15: R1_2.Pin_0, LED1_4.cathode
  N16: R1_3.Pin_0, LED1_5.cathode
  N17: R1_4.Pin_0, LED1_6.cathode
  N18: R1_5.Pin_0, LED1_7.cathode
  N19: R1_6.Pin_0, LED1.cathode
  N20: R1_7.Pin_0, LED1_8.cathode
  N21: R1_8.Pin_0, LED1_2.cathode
